# Fritzing sketch Arduino_max485_shield (saved by Fritzing 0.9.4)
circuit board: 7cm x 7cm
breadboards: 1

parts:
  485 = Module RS485 [package=board]
  Arduino = Arduino Pro Mini v13
  Phone_power = Screw terminal - 2 pins [package=THT]
  Relay_output = screw terminal, 3 pins
  rfid_reader = RFID-RC522-v2
  LedR = LED - 5mm [color="Red (633nm)" package="5 mm [THT]"]
  LedV = LED - 5mm [color="Green (560nm)" package="5 mm [THT]"]
  LedB = LED - 5mm [color="Blue (505nm)" package="5 mm [THT]"]
  R2 = Resistor [tolerance=±5% resistance=220 package=THT]
  R3 = Resistor [tolerance=±5% resistance=220 package=THT]
  R4 = Resistor [tolerance=±5% resistance=220 package=THT]
  Term = Resistor [tolerance=±5% resistance=120 package=THT]

nets:
  N1: 485.RO, Arduino.D1/RX
  N2: 485.RE, 485.DE, Arduino.D9_PWM
  N3: 485.DI, Arduino.D0/TX
  GND: 485.GND, Arduino.GND, Phone_power.pin1, Relay_output.pin3, rfid_reader.GND, LedR.cathode, LedV.cathode, LedB.cathode
  N4: 485.A, Term.Pin_0
  N5: 485.B, Term.Pin_1
  N6: 485.VCC, Arduino.RAW, Phone_power.pin2, Relay_output.pin2
  VCC: Arduino.VCC, rfid_reader.3.3V
  N7: Arduino.D13/SCK, rfid_reader.SCK
  N8: Arduino.D12/MISO, rfid_reader.MISO
  N9: Arduino.D11_PWM/MOSI, rfid_reader.MOSI
  N10: Arduino.D10_PWM/SS, rfid_reader.SDA
  N11: Arduino.D4, Relay_output.pin1
  N12: Arduino.D2, rfid_reader.RST
  N13: LedR.anode, R3.Pin_0
  N14: LedV.anode, R2.Pin_0
  N15: LedB.anode, R4.Pin_0

custom parts:
  Module RS485: RS-485 transceiver V1
  Arduino Pro Mini v13: It's blue! It's thin! It's the Arduino Pro Mini! SparkFun's minimal design approach to Arduino. This is a 5V Arduino running the 16MHz bootloader. Arduino Pro Mini does not come with connectors populated so that you can solder in any connector or wire with any orientation you need. We recommend first time Arduino users start with the Uno R3. It's a great board that will get you up and running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
  RFID-RC522-v2: A simple China made RFID-RC522 Reader; do check the pin labels, as this is a MFRC522 based clone.
